# Fritzing sketch Alternate Circuit (saved by Fritzing 0.9.3b)
breadboards: 1

parts:
  U1 = attiny85 [package=dip]
  R1 = Resistor [tolerance=±5% resistance=220 package="2010 [SMD]"]  # not connected
  R2 = Resistor [tolerance=±5% resistance=220 package="2010 [SMD]"]  # not connected
  R3 = Resistor [tolerance=±5% resistance=220 package="2010 [SMD]"]  # not connected
  R4 = Resistor [tolerance=±5% resistance=220 package="2010 [SMD]"]
  LED1 = smd LED [color="Red (633nm)" package="0603 [SMD]"]
  LED2 = smd LED [color="Red (633nm)" package="0603 [SMD]"]
  LED3 = smd LED [color="Red (633nm)" package="0603 [SMD]"]
  LED4 = smd LED [color="Red (633nm)" package="0603 [SMD]"]
  BAT1 = Battery Holders [package=battcom_20mm_pth]
  U2 = 555 Timer [package="DIP8 [THT]"]
  LED5 = smd LED [color="Red (633nm)" package="0603 [SMD]"]
  R5 = Resistor [tolerance=±5% resistance=220 package="2010 [SMD]"]

nets:
  N1: U1.Pin_1, U2.Threshold
  N2: U1.Pin_2, LED2.anode
  N3: U1.Pin_3, LED1.anode
  N4: U1.Pin_4, BAT1.-
  N5: U1.Pin_5, LED4.anode
  N6: U1.Pin_6, LED5.anode
  N7: U1.Pin_7, LED3.anode
  N8: U1.Pin_8, U2.Trigger
  N9: R4.Pin_1, R5.Pin_1
  N10: BAT1.+, U2.Discharge

notes:
  Heart Rate Sensor XD-58C*
